// Logisim project alu.circ as structural Verilog: 1 circuit, main circuit ALU
module ALU (
  input  [31:0] A,
  input  [31:0] B,
  input  [3:0] ALU_Op,
  output [31:0] Out
);

  wire [0:0] comparator_2_eq;
  wire [31:0] ADD, And, OR, RL, RR, SLL, SLR, SLT, SLTU, SRA, SRL, SUB, XOR;

  Multiplexer #(.width(32)) multiplexer_1 (.in0({32{1'b0}}), .in1(32'h1), .out(SLTU));  // open: sel, en
  Shifter #(.width(32)) shifter_1 (.in(A), .\dist (B[4:0]), .out(SLL));
  Shifter #(.width(32), .shift("lr")) shifter_2 (.in(A), .\dist (B[4:0]), .out(SRL));
  Shifter #(.width(32), .shift("ar")) shifter_3 (.in(A), .\dist (B[4:0]), .out(SRA));
  Shifter #(.width(32), .shift("rl")) shifter_4 (.in(A), .\dist (B[4:0]), .out(RL));
  Shifter #(.width(32), .shift("rr")) shifter_5 (.in(A), .\dist (B[4:0]), .out(RR));
  Comparator #(.width(32)) comparator_1 (.a(A), .b(B), .eq(SLT[0]));  // open: gt, lt
  Comparator #(.width(32), .mode("unsigned")) comparator_2 (.a(A), .b(B), .eq(comparator_2_eq[0]));  // open: gt, lt
  assign And = A & B;  // AND_Gate and_1, 32 bits wide
  assign OR = A | B;  // OR_Gate or_1, 32 bits wide
  assign XOR = A ^ B;  // XOR_Gate xor_1, 32 bits wide
  Adder #(.width(32)) adder_1 (.a(A), .b(B), .out(ADD));  // open: cin, cout
  Subtractor #(.width(32)) subtractor_1 (.a(A), .b(B), .out(SUB));  // open: bin, bout
  Multiplexer #(.select(4), .width(32)) multiplexer_2 (
    .in0(ADD), .in1(SUB), .in2(SLT), .in3(SLTU), .in4(SLL), .in5(SLR), .in6(SRA), .in7(RL), .in8(RR),
    .in9(And), .in10(OR), .in11(XOR), .out(Out), .sel(ALU_Op));  // open: in12, in13, in14, in15, en

  // Other names for the same wires on the sheet: s2_5min[4:0] = B[4:0]; Op[3:0] = ALU_Op

  // Notes on the sheet:
  //   Inputs
  //   NOTE
  //   Please do not modify/replace/move/change/delete/etc input and output pins
  //   Outputs
endmodule
